// Logisim project CPU.circ as structural Verilog
module ALU (
  input  [3:0] A,
  input  [3:0] B,
  input  [3:0] OP,
  input  [1:0] K,
  input  CF,
  output [3:0] Y,
  output [3:0] HIN,
  output Z,
  output C,
  output N,
  output V,
  output DIVZ
);

  wire and_2_out, and_3_out, CADD, CIN, D1, D2, D3, D4, D14, or_2_out, SC, SUBM, undriven, VADD, xnor_1_out,
       xor_3_out, YZ;
  wire [3:0] AN, BDIV, BP, MASK, NT, ORR, PH, PL, Q, REM_t, ROLY, RORY, S, SHLH, SHLL, SHRH, SHRY, SUBM4, XR;

  or or_1 (SUBM, D2, D3, D14);
  nor nor_1 (DIVZ, BP[0], BP[1], BP[2], BP[3]);
  Multiplexer #(.select(4), .width(4)) multiplexer_1 (
    .in0(S), .in1(S), .in2(S), .in3(S), .in4(PL), .in5(Q), .in6(AN), .in7(ORR), .in8(XR), .in9(NT),
    .in10(SHLL), .in11(SHRY), .in12(ROLY), .in13(RORY), .in14(S), .in15(S), .out({N, Y[2:0]}), .sel(OP));
  nor nor_2 (YZ, Y[0], Y[1], Y[2], N);
  assign SUBM4 = {{3{SUBM}}, SUBM};  // Bit_Extender bit_extender_1
  Decoder #(.enable("false"), .select(4)) decoder_1 (
    .out1(D1), .out2(D2), .out3(D3), .out4(D4), .out14(D14), .sel(OP));  // open: out0, out5, out6, out7, out8, out9, out10, out11, out12, out13, out15
  assign BP = B ^ SUBM4;  // XOR_Gate xor_1, 4 bits wide
  or or_2 (or_2_out, ~undriven, ~D4);  // OR_Gate
  and and_1 (Z, or_2_out, YZ);
  Multiplexer #(.width(4)) multiplexer_2 (.in0(B), .in1(4'b0001), .out(BDIV), .sel(DIVZ));
  Divider #(.width(4)) divider_1 (.a(A), .b(BDIV), .out(Q), .upper(4'b0000), .rem(REM_t));
  Multiplier #(.width(4)) multiplier_1 (.a(A), .b(B), .out(PL), .cin(4'b0000), .cout(PH));
  Multiplexer #(.select(4), .width(4)) multiplexer_3 (
    .in0(4'b0000), .in1(4'b0000), .in2(4'b0000), .in3(4'b0000), .in4(PH), .in5(REM_t), .in6(4'b0000),
    .in7(4'b0000), .in8(4'b0000), .in9(4'b0000), .in10(SHLH), .in11(SHRH), .in12(4'b0000), .in13(4'b0000),
    .in14(4'b0000), .in15(4'b0000), .out(HIN), .sel(OP));
  and and_2 (and_2_out, D1, CF);
  and and_3 (and_3_out, D3, ~CF);  // AND_Gate
  xor xor_2 (CADD, SUBM, SC);
  Multiplexer #(.select(4)) multiplexer_4 (
    .in0(CADD), .in1(CADD), .in2(CADD), .in3(CADD), .in4(D4), .in5(1'b0), .in6(1'b0), .in7(1'b0), .in8(1'b0),
    .in9(1'b0), .in10(D4), .in11(D4), .in12(1'b0), .in13(1'b0), .in14(CADD), .in15(1'b0), .out(C), .sel(OP));
  Adder #(.width(4)) adder_1 (.a(A), .b(BP), .out(S), .cin(CIN), .cout(SC));
  Multiplexer #(.select(2), .width(4)) multiplexer_5 (
    .in0(4'b0000), .in1(4'b0001), .in2(4'b0011), .in3(4'b0111), .out(MASK), .sel(K));
  or or_3 (CIN, and_2_out, and_3_out, D2, D14);
  xnor xnor_1 (xnor_1_out, A[3], BP[3]);
  xor xor_3 (xor_3_out, A[3], S[3]);
  or or_4 (D4, HIN[0], HIN[1], HIN[2], HIN[3]);
  and and_4 (VADD, xnor_1_out, xor_3_out);
  assign SHRH = A & MASK;  // AND_Gate and_5, 4 bits wide
  assign AN = A & B;  // AND_Gate and_6, 4 bits wide
  assign ORR = A | B;  // OR_Gate or_5, 4 bits wide
  assign XR = A ^ B;  // XOR_Gate xor_4, 4 bits wide
  assign NT = ~A;  // NOT_Gate not_1, 4 bits wide
  Shifter shifter_1 (.in({4'b0000, A}), .\dist ({1'b0, K}), .out({SHLH, SHLL}));
  Shifter #(.shift("lr"), .width(4)) shifter_2 (.in(A), .\dist (K), .out(SHRY));
  Multiplexer #(.select(4)) multiplexer_6 (
    .in0(VADD), .in1(VADD), .in2(VADD), .in3(VADD), .in4(D4), .in5(DIVZ), .in6(1'b0), .in7(1'b0), .in8(1'b0),
    .in9(1'b0), .in10(D4), .in11(1'b0), .in12(1'b0), .in13(1'b0), .in14(VADD), .in15(1'b0), .out(V), .sel(OP));
  Shifter #(.shift("rl"), .width(4)) shifter_3 (.in(A), .\dist (K), .out(ROLY));
  Shifter #(.shift("rr"), .width(4)) shifter_4 (.in(A), .\dist (K), .out(RORY));

  assign Y[3] = N;

  // Other names for the same wires on the sheet: HNZ = D4
endmodule

module REGFILE (
  input  CLK,
  input  RESET,
  input  [1:0] RD,
  input  [1:0] RS,
  input  [3:0] WD,
  input  WE,
  output [3:0] A,
  output [3:0] B,
  output [3:0] R0,
  output [3:0] R1,
  output [3:0] R2,
  output [3:0] R3
);

  wire L0, L1, L2, L3, or_1_out, or_2_out, or_3_out, or_4_out;
  wire [3:0] WDR;

  or or_1 (or_1_out, L0, RESET);
  or or_2 (or_2_out, L1, RESET);
  or or_3 (or_3_out, L2, RESET);
  or or_4 (or_4_out, L3, RESET);
  Multiplexer #(.width(4)) multiplexer_1 (.in0(WD), .in1(4'b0000), .out(WDR), .sel(RESET));
  Register #(.width(4)) register_1 (.D(WDR), .en(or_1_out), .clk(CLK), .Q(R0), .clr(1'b0));
  Register #(.width(4)) register_2 (.D(WDR), .en(or_2_out), .clk(CLK), .Q(R1), .clr(1'b0));
  Register #(.width(4)) register_3 (.D(WDR), .en(or_3_out), .clk(CLK), .Q(R2), .clr(1'b0));
  Register #(.width(4)) register_4 (.D(WDR), .en(or_4_out), .clk(CLK), .Q(R3), .clr(1'b0));
  Decoder #(.select(2)) decoder_1 (.out0(L0), .out1(L1), .out2(L2), .out3(L3), .sel(RD), .en(WE));
  Multiplexer #(.select(2), .width(4)) multiplexer_2 (.in0(R0), .in1(R1), .in2(R2), .in3(R3), .out(A), .sel(RD));
  Multiplexer #(.select(2), .width(4)) multiplexer_3 (.in0(R0), .in1(R1), .in2(R2), .in3(R3), .out(B), .sel(RS));
endmodule
